// Logisim project Aufgabe_Uebung_3.circ as structural Verilog: 1 circuit, main circuit main
module main (
  input  B_1,
  input  B_2,
  input  B_3,
  output out_4,
  output out_5
);

  wire and_1_out, and_2_out, and_3_out, and_4_out, and_5_out, and_6_out, and_7_out;

  and and_1 (and_1_out, ~B_1, B_1, B_2, B_3);  // AND_Gate
  and and_2 (and_2_out, B_1, B_2, ~B_2, B_3);  // AND_Gate
  and and_3 (and_3_out, B_1, B_2, ~B_3);  // AND_Gate
  and and_4 (and_4_out, B_1, B_2, B_3);
  and and_5 (and_5_out, B_2, B_3);
  and and_6 (and_6_out, B_1, B_3);
  and and_7 (and_7_out, B_1, B_2);
  or or_1 (out_4, and_1_out, and_2_out, and_3_out, and_4_out);
  or or_2 (out_5, and_5_out, and_6_out, and_7_out);

  // Notes on the sheet:
  //   Normalform
  //   vereinfachte Form
endmodule
